// Logisim project ALU.circ as structural Verilog: 1 circuit, main circuit ALU
module ALU (
  input  [31:0] A,
  input  [31:0] B,
  input  [4:0] Shift,
  input  [3:0] Codop,
  input  CarryIn,
  output [31:0] S,
  output [3:0] Flags
);

  wire adder_1_cout, adder_2_cout, and_4_out, and_5_out, and_6_out, and_7_out, asr_lsr, bitselector_4_out,
       bitselector_5_out, bitselector_6_out, bitselector_7_out, bitselector_8_out, bitselector_9_out,
       bitselector_10_out, bitselector_11_out, bitselector_12_out, bitselector_13_out, lsl_c, not_1_out,
       not_2_out, not_3_out, result, subtractor_1_bout, subtractor_2_bout, xnor_1_out, xnor_2_out, xor_2_out,
       xor_3_out, xor_4_out, xor_5_out, xor_6_out, xor_7_out;
  wire [4:0] negator_2_out, subtractor_3_out;
  wire [31:0] adder_1_out, and_1_out, and_3_out, cmm, cmp, multiplexer_3_out, multiplier_1_out,
       negator_1_out, not_4_out, or_1_out, shifter_1_out, shifter_2_out, shifter_3_out, shifter_4_out,
       subtractor_1_out, tst, xor_1_out;

  assign and_1_out = A & B;  // AND_Gate and_1, 32 bits wide
  assign xor_1_out = A ^ B;  // XOR_Gate xor_1, 32 bits wide
  Shifter #(.width(32)) shifter_1 (.in(B), .\dist (Shift), .out(shifter_1_out));
  Shifter #(.shift("lr"), .width(32)) shifter_2 (.in(B), .\dist (Shift), .out(shifter_2_out));
  Shifter #(.shift("ar"), .width(32)) shifter_3 (.in(B), .\dist (Shift), .out(shifter_3_out));
  Adder #(.width(32)) adder_1 (.a(A), .b(B), .out(adder_1_out), .cin(CarryIn), .cout(adder_1_cout));
  not not_1 (not_1_out, CarryIn);
  Subtractor #(.width(32)) subtractor_1 (
    .a(B), .b(A), .out(subtractor_1_out), .bin(not_1_out), .bout(subtractor_1_bout));
  not not_2 (not_2_out, subtractor_1_bout);
  Shifter #(.shift("rr"), .width(32)) shifter_4 (.in(B), .\dist (Shift), .out(shifter_4_out));
  assign tst = A & B;  // AND_Gate and_2, 32 bits wide
  Negator #(.width(32)) negator_1 (.in(A), .out(negator_1_out));
  Subtractor #(.width(32)) subtractor_2 (.a(B), .b(A), .out(cmp), .bout(subtractor_2_bout));  // open: bin
  not not_3 (not_3_out, subtractor_2_bout);
  Adder #(.width(32)) adder_2 (.a(A), .b(B), .out(cmm), .cout(adder_2_cout));  // open: cin
  assign or_1_out = A | B;  // OR_Gate or_1, 32 bits wide
  Multiplier #(.width(32)) multiplier_1 (.a(A), .b(B), .out(multiplier_1_out));  // open: cin, cout
  assign and_3_out = B & ~A;  // AND_Gate and_3, 32 bits wide
  assign not_4_out = ~A;  // NOT_Gate not_4, 32 bits wide
  Multiplexer #(.enable("false"), .select(4), .width(32)) multiplexer_1 (
    .in0(and_1_out), .in1(xor_1_out), .in2(shifter_1_out), .in3(shifter_2_out), .in4(shifter_3_out),
    .in5(adder_1_out), .in6(subtractor_1_out), .in7(shifter_4_out), .in8(B), .in9(negator_1_out), .in10(B),
    .in11(B), .in12(or_1_out), .in13(multiplier_1_out), .in14(and_3_out), .in15(not_4_out), .out(S),
    .sel(Codop));
  BitSelector #(.width(32)) bitselector_1 (.in(S), .out(result), .sel({5{1'b1}}));
  Subtractor #(.width(5)) subtractor_3 (.a(Shift), .b(5'b00001), .out(subtractor_3_out));  // open: bin, bout
  Multiplexer #(.enable("false"), .select(4)) multiplexer_2 (
    .in0(1'b0), .in1(1'b0), .in2(lsl_c), .in3(asr_lsr), .in4(asr_lsr), .in5(adder_1_cout), .in6(not_2_out),
    .in7(Flags[3]), .in8(1'b0), .in9(1'b0), .in10(not_3_out), .in11(adder_2_cout), .in12(1'b0), .in13(1'b0),
    .in14(1'b0), .in15(1'b0), .out(Flags[1]), .sel(Codop));
  BitSelector #(.width(32)) bitselector_2 (.in(B), .out(lsl_c), .sel(negator_2_out));
  Negator #(.width(5)) negator_2 (.in(Shift), .out(negator_2_out));
  BitSelector #(.width(32)) bitselector_3 (.in(B), .out(asr_lsr), .sel(subtractor_3_out));
  Multiplexer #(.enable("false"), .select(4), .width(32)) multiplexer_3 (
    .in0(S), .in1(S), .in2(S), .in3(S), .in4(S), .in5(S), .in6(S), .in7(S), .in8(tst), .in9(S), .in10(cmp),
    .in11(cmm), .in12(S), .in13(S), .in14(S), .in15(S), .out(multiplexer_3_out), .sel(Codop));
  Comparator #(.width(32)) comparator_1 (
    .a(multiplexer_3_out), .b({32{1'b0}}), .eq(Flags[2]), .lt(Flags[3]));  // open: gt
  BitSelector #(.width(32)) bitselector_4 (.in(A), .out(bitselector_4_out), .sel({5{1'b1}}));
  BitSelector #(.width(32)) bitselector_5 (.in(cmp), .out(bitselector_5_out), .sel({5{1'b1}}));
  BitSelector #(.width(32)) bitselector_6 (.in(A), .out(bitselector_6_out), .sel({5{1'b1}}));
  BitSelector #(.width(32)) bitselector_7 (.in(B), .out(bitselector_7_out), .sel({5{1'b1}}));
  BitSelector #(.width(32)) bitselector_8 (.in(cmm), .out(bitselector_8_out), .sel({5{1'b1}}));
  BitSelector #(.width(32)) bitselector_9 (.in(A), .out(bitselector_9_out), .sel({5{1'b1}}));
  BitSelector #(.width(32)) bitselector_10 (.in(B), .out(bitselector_10_out), .sel({5{1'b1}}));
  BitSelector #(.width(32)) bitselector_11 (.in(A), .out(bitselector_11_out), .sel({5{1'b1}}));
  BitSelector #(.width(32)) bitselector_12 (.in(B), .out(bitselector_12_out), .sel({5{1'b1}}));
  BitSelector #(.width(32)) bitselector_13 (.in(B), .out(bitselector_13_out), .sel({5{1'b1}}));
  xor xor_2 (xor_2_out, bitselector_5_out, bitselector_7_out);
  xor xor_3 (xor_3_out, bitselector_6_out, bitselector_7_out);
  xor xor_4 (xor_4_out, bitselector_8_out, bitselector_10_out);
  xnor xnor_1 (xnor_1_out, bitselector_9_out, bitselector_10_out);
  xor xor_5 (xor_5_out, result, bitselector_12_out);
  xnor xnor_2 (xnor_2_out, bitselector_11_out, bitselector_12_out);
  xor xor_6 (xor_6_out, result, bitselector_13_out);
  xor xor_7 (xor_7_out, bitselector_4_out, bitselector_13_out);
  and and_4 (and_4_out, xor_4_out, xnor_1_out);
  and and_5 (and_5_out, xor_5_out, xnor_2_out);
  and and_6 (and_6_out, xor_6_out, xor_7_out);
  and and_7 (and_7_out, xor_2_out, xor_3_out);
  Multiplexer #(.enable("false"), .select(4)) multiplexer_4 (
    .in0(1'b0), .in1(1'b0), .in2(1'b0), .in3(1'b0), .in4(1'b0), .in5(and_5_out), .in6(and_6_out), .in7(1'b0),
    .in8(1'b0), .in9(1'b0), .in10(and_7_out), .in11(and_4_out), .in12(1'b0), .in13(1'b0), .in14(1'b0),
    .in15(1'b0), .out(Flags[0]), .sel(Codop));

  // Other names for the same wires on the sheet: CO[3:0] = Codop; V = Flags[0]; C = Flags[1]; Z = Flags[2];
  //   N = Flags[3]

  // Notes on the sheet:
  //   Note: for ROR, C = N
  //   Note 2: assume that shift > 0 for LSL and LSR
  //   montage pour V
endmodule
