// Logisim project Ctl_Conditional.circ as structural Verilog: 1 circuit, main circuit Conditional
module Conditional (
  input  [15:0] Instruction,
  input  Z,
  input  Enable,
  input  C,
  input  N,
  input  V,
  output [10:0] Offset,
  output Verified
);

  wire CCouLO, GE, GT, HI, LE, LS, LT, multiplexer_1_out, NE, not_1_out, or_3_out, PL, VC;
  wire [10:0] bit_extender_1_out, multiplexer_2_out;

  not not_1 (not_1_out, Z);
  not not_2 (NE, Z);
  and and_1 (HI, not_1_out, C);
  not not_3 (CCouLO, C);
  or or_1 (LS, CCouLO, Z);
  not not_4 (PL, N);
  not not_5 (VC, V);
  and and_2 (GT, NE, GE);
  or or_2 (LE, Z, LT);
  not not_6 (LT, GE);
  xnor xnor_1 (GE, N, V);
  Multiplexer #(.enable("false"), .select(4)) multiplexer_1 (
    .in0(Z), .in1(NE), .in2(C), .in3(CCouLO), .in4(N), .in5(PL), .in6(V), .in7(VC), .in8(HI), .in9(LS),
    .in10(GE), .in11(LT), .in12(GT), .in13(LE), .in14(1'b1), .out(multiplexer_1_out), .sel(Instruction[11:8]));  // open: in15
  assign bit_extender_1_out = {{3{Instruction[7]}}, Instruction[7:0]};  // Bit_Extender bit_extender_1
  Multiplexer #(.enable("false"), .width(11)) multiplexer_2 (
    .in0(bit_extender_1_out), .in1(Instruction[10:0]), .out(multiplexer_2_out), .sel(Instruction[13]));
  or or_3 (or_3_out, Instruction[13], multiplexer_1_out);
  Multiplexer #(.enable("false"), .width(11)) multiplexer_3 (
    .in0({11{1'b0}}), .in1(multiplexer_2_out), .out(Offset), .sel(Verified));
  and and_3 (Verified, Enable, or_3_out);

  // Other names for the same wires on the sheet: CSouHS = C; EQ = Z; Imm8[7:0] = Instruction[7:0];
  //   Imm11[10:0] = Instruction[10:0]; Cond[3:0] = Instruction[11:8]; InBranch = Instruction[13]; MI = N; VS = V

  // Notes on the sheet:
  //   NE AND CSouHS
  //   CCouLO OU EQ
  //   NE AND GE
  //   EQ ou LT
  //   c == 1, retenu
  //   c == 0, pas de retenu
  //   C == 0 et Z == 1, inferieur ou égal
  //   Z == 1 ou N != V, inf ou égal
  //   Z == 1, égalité
  //   z == 0, difference
  //   N == 1, négatif
  //   N == 0, positif ou nul
  //   V == 1, overflow
  //   V == 0, no overflow
  //   C == 1 et Z == 0 , supérieur 
  //   N == V, sup ou égal
  //   N != V, Inferieur
  //   Z == 0 et N == V, superieur
endmodule
