// Logisim project Ctl_Data_Processing.circ as structural Verilog: 1 circuit, main circuit Data_Processing
module Data_Processing (
  input  Enable,
  input  [15:0] Instruction,
  output [2:0] Rd,
  output [2:0] Rn,
  output [2:0] Rm,
  output [3:0] ALU_Opcode,
  output [3:0] Flags_Update_Mask
);

  wire and_2_out, and_3_out, OpF;
  wire [1:1] not_1_out;
  wire [3:0] bit_extender_2_out;
  wire [15:0] bit_extender_1_out;
  wire [15:3] NewI;

  assign bit_extender_1_out = {{15{Enable}}, Enable};  // Bit_Extender bit_extender_1
  assign {NewI[15:10], ALU_Opcode, NewI[5:3], Rd} = bit_extender_1_out & Instruction;  // AND_Gate and_1, 16 bits wide
  Multiplexer #(.enable("false"), .select(4)) multiplexer_1 (
    .in0(1'b0), .in1(1'b0), .in2(1'b0), .in3(1'b0), .in4(1'b0), .in5(1'b1), .in6(1'b1), .in7(1'b0),
    .in8(1'b0), .in9(1'b1), .in10(1'b1), .in11(1'b1), .in12(1'b0), .in13(1'b0), .in14(1'b0), .in15(1'b0),
    .out(OpF), .sel(ALU_Opcode));
  and and_2 (and_2_out, ALU_Opcode[0], ~ALU_Opcode[1], ALU_Opcode[3]);  // AND_Gate
  and and_3 (and_3_out, ALU_Opcode[2], and_2_out);
  Multiplexer #(.enable("false"), .select(4), .width(3)) multiplexer_2 (
    .in0(Rd), .in1(Rd), .in2(Rd), .in3(Rd), .in4(Rd), .in5(Rd), .in6(Rd), .in7(Rd), .in8(Rd),
    .in9(NewI[5:3]), .in10(Rd), .in11(Rd), .in12(Rd), .in13(NewI[5:3]), .in14(Rd), .in15(Rd), .out(Rn),
    .sel(ALU_Opcode));
  not not_1 (not_1_out[1], and_3_out);
  assign Flags_Update_Mask = {2'b11, not_1_out[1], OpF} & bit_extender_2_out;  // AND_Gate and_4, 4 bits wide
  assign bit_extender_2_out = {{3{Enable}}, Enable};  // Bit_Extender bit_extender_2
  Multiplexer #(.enable("false"), .select(4), .width(3)) multiplexer_3 (
    .in0(NewI[5:3]), .in1(NewI[5:3]), .in2(NewI[5:3]), .in3(NewI[5:3]), .in4(NewI[5:3]), .in5(NewI[5:3]),
    .in6(NewI[5:3]), .in7(NewI[5:3]), .in8(NewI[5:3]), .in9(NewI[5:3]), .in10(NewI[5:3]), .in11(NewI[5:3]),
    .in12(NewI[5:3]), .in13(Rd), .in14(NewI[5:3]), .in15(NewI[5:3]), .out(Rm), .sel(ALU_Opcode));

  // Other names for the same wires on the sheet: E = Enable; NewI (some bits) = {ALU_Opcode, Rd}; t1[2:0] = Rd;
  //   t2[2:0] = NewI[5:3]

  // Notes on the sheet:
  //   ANDS t1 t2
  //   2-0 t1 
  //   5-3 t2
  //   9-6 ALU
  //   Pull output low on Enable = 0
  //   Note 2: RSB instruction has Rn as 1st operand.
  //   MUL instruction has Rn as 1st operand and Rdm as 2nd operand
  //   For simplification purposes, Rm is used for 1st operand both here and in the ALU.
  //   Note: instructions that does not save the result will still have the second operand as the destination register, the ALU will copy the second register to the destination register
endmodule
