// Logisim project Ctl_Load_Store.circ as structural Verilog: 1 circuit, main circuit Load_Store
module Load_Store (
  input  Enable,
  input  [15:0] Instruction,
  input  Clk,
  input  Reset,
  input  [31:0] Stack_Pointer,
  output Load,
  output Store,
  output PC_Hold,
  output [2:0] Rmd,
  output [31:0] RAM_Addr
);

  wire and_4_out, d_ff_1_q, d_ff_1_qn, or_1_out;
  wire [2:0] bit_extender_3_out;
  wire [31:0] adder_1_out, bit_extender_2_out, Imm8;

  assign Imm8 = {{24{Instruction[7]}}, Instruction[7:0]};  // Bit_Extender bit_extender_1
  Adder #(.width(32)) adder_1 (.a(Imm8), .b(Stack_Pointer), .out(adder_1_out));  // open: cin, cout
  assign bit_extender_2_out = {{31{Enable}}, Enable};  // Bit_Extender bit_extender_2
  assign Rmd = Instruction[10:8] & bit_extender_3_out;  // AND_Gate and_1, 3 bits wide
  assign bit_extender_3_out = {{2{Enable}}, Enable};  // Bit_Extender bit_extender_3
  assign RAM_Addr = adder_1_out & bit_extender_2_out;  // AND_Gate and_2, 32 bits wide
  and and_3 (Store, ~Instruction[11], Enable);  // AND_Gate
  and and_4 (and_4_out, ~d_ff_1_q, Instruction[11]);  // AND_Gate
  D_Flip_Flop #(.trigger("falling")) d_ff_1 (
    .D(and_4_out), .clk(Clk), .Q(d_ff_1_q), .Qn(d_ff_1_qn), .reset(or_1_out));  // open: preset
  or or_1 (or_1_out, ~Enable, Reset, ~Instruction[11]);  // OR_Gate
  and and_5 (Load, Enable, Instruction[11], d_ff_1_q);
  and and_6 (PC_Hold, Enable, d_ff_1_qn, Instruction[11]);

  // Other names for the same wires on the sheet: E = Enable; bit11 = Instruction[11]

  // Notes on the sheet:
  //   Instruction: pull=down
  //   Delay load and hold PC for 1 cycle for the RAM to send out requested data 
endmodule
