// Logisim project Ctl_SP_Address.circ as structural Verilog: 1 circuit, main circuit SP_Address
module SP_Address (
  input  [31:0] Stack_Pointer,
  input  [15:0] Instruction,
  input  Enable,
  output [31:0] New_Stack_Pointer,
  output Write_Enable
);

  wire RV;
  wire [15:0] and_1_out, bit_extender_1_out;
  wire [31:0] adder_1_out, bit_extender_2_out, bit_extender_3_out, multiplexer_1_out, subtractor_1_out;

  assign bit_extender_1_out = {{15{Enable}}, Enable};  // Bit_Extender bit_extender_1
  assign {and_1_out[15:8], RV, and_1_out[6:0]} = Instruction & bit_extender_1_out;  // AND_Gate and_1, 16 bits wide
  assign bit_extender_2_out = {{25{1'b0}}, and_1_out[6:0]};  // Bit_Extender bit_extender_2
  Adder #(.width(32)) adder_1 (.a(bit_extender_2_out), .b(Stack_Pointer), .out(adder_1_out));  // open: cin, cout
  Subtractor #(.width(32)) subtractor_1 (
    .a(Stack_Pointer), .b(bit_extender_2_out), .out(subtractor_1_out));  // open: bin, bout
  Multiplexer #(.enable("false"), .width(32)) multiplexer_1 (
    .in0(adder_1_out), .in1(subtractor_1_out), .out(multiplexer_1_out), .sel(RV));
  assign bit_extender_3_out = {{31{Enable}}, Enable};  // Bit_Extender bit_extender_3
  assign New_Stack_Pointer = multiplexer_1_out & bit_extender_3_out;  // AND_Gate and_2, 32 bits wide

  assign Write_Enable = Enable;

  // Notes on the sheet:
  //   Pull output low on Enable = 0
endmodule
