// Logisim project Ctl_Shift_Add_Sub_Mov.circ as structural Verilog: 1 circuit, main circuit Shift_Add_Sub_Mov
module Shift_Add_Sub_Mov (
  input  Enable,
  input  [15:0] Instruction,
  output [3:0] Flags_Update_Mask,
  output [4:0] Imm5,
  output [2:0] Rn,
  output [2:0] Rm,
  output [3:0] ALU_Opcode,
  output Imm32_Enable,
  output [2:0] Rd,
  output Carry,
  output [31:0] Imm32
);

  wire ADDi_3bit, ADDi_8bit, ADDorSUB, ADDr, and_1_out, and_2_out, and_7_out, and_11_out, and_13_out,
       and_14_out, and_15_out, ASRi, CMPi, comparator_1_eq, LSLi, LSRi, MOVi, or_1_out, or_2_out, or_3_out,
       or_4_out, or_5_out, or_6_out, SUBi_3bit, SUBi_8bit, SUBr;
  wire [0:0] and_16_out;
  wire [1:0] Montage;
  wire [2:0] Imm3;
  wire [3:0] adder_1_out, adder_2_out, ALU, bit_extender_6_out, multiplexer_3_out;
  wire [7:0] Imm8;
  wire [15:0] and_3_out, and_4_out, and_5_out, and_6_out, and_8_out, bit_extender_1_out, bit_extender_2_out,
       bit_extender_3_out, bit_extender_4_out, bit_extender_5_out, bit_extender_7_out, NewI;
  wire [31:0] bit_extender_8_out, bit_extender_9_out, multiplexer_1_out, negator_1_out;

  or or_1 (or_1_out, LSLi, LSRi, ASRi);
  or or_2 (or_2_out, ADDr, SUBr);
  or or_3 (or_3_out, ADDi_3bit, SUBi_3bit);
  assign bit_extender_1_out = {{15{or_1_out}}, or_1_out};  // Bit_Extender bit_extender_1
  and and_1 (and_1_out, ADDorSUB, or_2_out);
  and and_2 (and_2_out, ADDorSUB, or_3_out);
  or or_4 (or_4_out, MOVi, CMPi);
  or or_5 (or_5_out, ADDi_8bit, SUBi_8bit);
  or or_6 (or_6_out, ADDi_3bit, SUBi_3bit);
  assign {and_3_out[15:11], Imm5, and_3_out[5:0]} = bit_extender_1_out & NewI;  // AND_Gate and_3, 16 bits wide
  assign bit_extender_2_out = {{15{and_1_out}}, and_1_out};  // Bit_Extender bit_extender_2
  assign and_4_out = bit_extender_2_out & NewI;  // AND_Gate and_4, 16 bits wide
  assign bit_extender_3_out = {{15{and_2_out}}, and_2_out};  // Bit_Extender bit_extender_3
  assign bit_extender_4_out = {{15{or_4_out}}, or_4_out};  // Bit_Extender bit_extender_4
  assign and_5_out = bit_extender_4_out & NewI;  // AND_Gate and_5, 16 bits wide
  assign bit_extender_5_out = {{15{or_5_out}}, or_5_out};  // Bit_Extender bit_extender_5
  assign and_6_out = bit_extender_5_out & NewI;  // AND_Gate and_6, 16 bits wide
  and and_7 (and_7_out, ADDorSUB, or_6_out);
  assign {and_8_out[15:9], Imm3, and_8_out[5:0]} = bit_extender_3_out & NewI;  // AND_Gate and_8, 16 bits wide
  or or_7 (Imm32_Enable, and_7_out, MOVi, CMPi, ADDi_8bit, SUBi_8bit);
  assign bit_extender_6_out = {{3{Enable}}, Enable};  // Bit_Extender bit_extender_6
  assign Flags_Update_Mask = bit_extender_6_out & {2'b11, Montage};  // AND_Gate and_9, 4 bits wide
  assign Imm8 = and_6_out[7:0] | and_5_out[7:0];  // OR_Gate or_8, 8 bits wide
  assign bit_extender_7_out = {{15{Enable}}, Enable};  // Bit_Extender bit_extender_7
  assign NewI = Instruction & bit_extender_7_out;  // AND_Gate and_10, 16 bits wide
  assign Rm = and_3_out[5:3] | and_4_out[8:6];  // OR_Gate or_9, 3 bits wide
  assign bit_extender_8_out = {{29{1'b0}}, Imm3};  // Bit_Extender bit_extender_8
  assign bit_extender_9_out = {{24{1'b0}}, Imm8};  // Bit_Extender bit_extender_9
  Negator #(.width(32)) negator_1 (.in(bit_extender_9_out), .out(negator_1_out));
  assign Rd = and_3_out[2:0] | and_4_out[2:0] | and_8_out[2:0] | and_5_out[10:8] | and_6_out[10:8];  // OR_Gate or_10, 3 bits wide
  assign Rn = and_4_out[5:3] | and_8_out[5:3] | and_3_out[5:3] | and_6_out[10:8];  // OR_Gate or_11, 3 bits wide
  Comparator #(.width(4)) comparator_1 (.a(4'b0110), .b(ALU), .eq(comparator_1_eq));  // open: gt, lt
  Multiplexer #(.enable("false"), .width(32)) multiplexer_1 (
    .in0(bit_extender_9_out), .in1(negator_1_out), .out(multiplexer_1_out), .sel(MOVi));
  and and_11 (and_11_out, ~NewI[11], ~NewI[12]);  // AND_Gate
  and and_12 (Carry, Enable, comparator_1_eq);
  Multiplexer #(.enable("false"), .width(32)) multiplexer_2 (
    .in0(bit_extender_8_out), .in1(multiplexer_1_out), .out(Imm32), .sel(NewI[13]));
  and and_13 (and_13_out, NewI[11], NewI[12]);
  or or_12 (Montage[1], ~NewI[13], NewI[12], NewI[11]);  // OR_Gate
  and and_14 (and_14_out, NewI[13], Montage[1]);
  or or_13 (Montage[0], and_14_out, and_13_out);
  Decoder #(.select(3)) decoder_1 (
    .out0(LSLi), .out1(LSRi), .out2(ASRi), .out3(ADDorSUB), .out4(MOVi), .out5(CMPi), .out6(ADDi_8bit),
    .out7(SUBi_8bit), .sel(NewI[13:11]));  // open: en
  Decoder #(.select(2)) decoder_2 (
    .out0(ADDr), .out1(SUBr), .out2(ADDi_3bit), .out3(SUBi_3bit), .sel(NewI[10:9]));  // open: en
  and and_15 (and_15_out, Instruction[11], Instruction[12]);
  Adder #(.width(4)) adder_1 (.a(4'b0010), .b(Instruction[14:11]), .out(adder_1_out), .cin(1'b0));  // open: cout
  and and_16 (and_16_out[0], Instruction[9], and_15_out);
  Multiplexer #(.enable("false"), .select(2), .width(4)) multiplexer_3 (
    .in0(4'b1001), .in1(4'b1010), .in2(4'b0101), .in3(4'b0110), .out(multiplexer_3_out),
    .sel(Instruction[12:11]));
  Pull_Resistor pull_resistor_1 (.node(ALU_Opcode));
  assign ALU_Opcode = Enable ? ALU : 4'bz;  // Controlled_Buffer controlled_buffer_1
  Adder #(.width(4)) adder_2 (
    .a({3'b000, and_16_out[0]}), .b(adder_1_out), .out(adder_2_out), .cin(1'b0));  // open: cout
  Multiplexer #(.enable("false"), .width(4)) multiplexer_4 (
    .in0(adder_2_out), .in1(multiplexer_3_out), .out(ALU), .sel(Instruction[13]));

  // Other names for the same wires on the sheet: E = Enable; I[15:0] = Instruction

  // Notes on the sheet:
  //   Rm 8-6 , Rn 5-3 , Rd 2-0
  //   imm3 8-6, Rn 5-3, Rd 2-0
  //   imm3 8-6, Rn 5-3, Rd 2-0
  //   Imm5 10-6 , Rm 5-3 , Rd 2-0
  //   Rd 10-8 , Imm8 7-0
  //   Note 3: Imm32_Enable forces the use of the immediate for Rm register
  //   Note: ALU uses Rn register for shifts. Use Rn instead of Rm for shifts (immediate) here too
  //   Note 2: MOV uses RSB ALU opcode with Imm8 reversed so that it is copied to output register
  //   Pull output low on Enable = 0
  //   6 correspond au opération SUB
  //   only ADD and SUB use Rm
  //   Enable carry for SUB since it is reversed in ALU
  //   ALU will use Imm32 instead of Rm
  //   (00)
  //   (01)
  //   (10)
  //   (11)
  //   0 1 1 0 0
  //   0 1 1 0 1
  //   0 1 1 1 0
  //   0 1 1 1 1
  //   0 0 0
  //   0 0 1
  //   0 1 0
  //   0 1 1
  //   1 0 0
  //   1 0 1
  //   1 1 0
  //   1 1 1 
endmodule
